// Logisim project Nano8.circ as structural Verilog
module Registers (
  input  D,
  input  RES,
  input  CLK,
  input  [7:0] P0,
  input  R,
  input  [2:0] R_SEL,
  output [7:0] P1,
  output [7:0] P2
);

  wire demultiplexer_1_out0, demultiplexer_1_out1, demultiplexer_1_out2, demultiplexer_1_out3,
       demultiplexer_1_out4, demultiplexer_1_out5, demultiplexer_1_out6, demultiplexer_1_out7, E1E, E2E, O2E;
  wire [7:0] register_1_q, register_2_q;

  not not_1 (E1E, R_SEL[0]);
  Demultiplexer #(.select(3)) demultiplexer_1 (
    .out0(demultiplexer_1_out0), .out1(demultiplexer_1_out1), .out2(demultiplexer_1_out2),
    .out3(demultiplexer_1_out3), .out4(demultiplexer_1_out4), .out5(demultiplexer_1_out5),
    .out6(demultiplexer_1_out6), .out7(demultiplexer_1_out7), .in(R), .sel(R_SEL));
  Register register_1 (.D(P0), .en(demultiplexer_1_out0), .clk(CLK), .Q(register_1_q), .clr(RES));
  Register register_2 (.D(P0), .en(demultiplexer_1_out1), .clk(CLK), .Q(register_2_q), .clr(RES));
  Register register_3 (.D(P0), .en(demultiplexer_1_out2), .clk(RES), .Q(register_1_q), .clr(RES));
  Register register_4 (.D(P0), .en(demultiplexer_1_out3), .clk(CLK), .Q(register_2_q), .clr(RES));
  Register register_5 (.D(P0), .en(demultiplexer_1_out4), .clk(CLK), .Q(register_1_q), .clr(RES));
  Register register_6 (.D(P0), .en(demultiplexer_1_out5), .clk(CLK), .Q(register_2_q), .clr(RES));
  Register register_7 (.D(P0), .en(demultiplexer_1_out6), .clk(CLK), .Q(register_1_q), .clr(RES));
  Register register_8 (.D(P0), .en(demultiplexer_1_out7), .clk(CLK), .Q(register_2_q), .clr(RES));
  and and_1 (E2E, D, R_SEL[0]);
  and and_2 (O2E, ~D, E1E);  // AND_Gate
  assign P1 = E1E ? register_1_q : 8'bz;  // Controlled_Buffer controlled_buffer_1
  assign P1 = R_SEL[0] ? register_2_q : 8'bz;  // Controlled_Buffer controlled_buffer_2
  assign P2 = E2E ? register_1_q : 8'bz;  // Controlled_Buffer controlled_buffer_3
  assign P2 = O2E ? register_2_q : 8'bz;  // Controlled_Buffer controlled_buffer_4
  Pull_Resistor pull_resistor_1 (.node(P1));
  Pull_Resistor pull_resistor_2 (.node(P2));

  // Other names for the same wires on the sheet: ODD = E1E; EVEN = R_SEL[0]; O1E = R_SEL[0]
endmodule
